# Fritzing sketch HenHouse (saved by Fritzing 0.9.4)

parts:
  Composant1 = Adafruit USB DC Solar LiPo Charger [part_number="Adafruit #390"]
  Composant2 = Lithium Ion Battery Pack 3.7V 4400mAh [part_number=354]  # not connected
  Composant3 = Adafruit Feather 32u4 RFM9xW LoRa [part_number="Adafruit #3078 and Adafruit #3079"]
  U1 = DC-DC_CONVERTER [package=dc-dc_converter]  # not connected
  D1 = SOLAR-IXYS [package=solarbit-12x1]  # not connected
  M1 = DC Motor
  S2 = Reed switch [package=THT]
  DS1 = DS18B20 1-Wire Temperature Sensor [part_number=DS18B20]
  DS2 = DS18B20 1-Wire Temperature Sensor [part_number=DS18B20]  # not connected
  DS3 = DS18B20 1-Wire Temperature Sensor [part_number=DS18B20]  # not connected
  DS4 = DS18B20 1-Wire Temperature Sensor [part_number=DS18B20]
  R2 = Resistor [tolerance=±5% resistance=3.3k package="0603 [SMD]"]
  Composant4 = Motor Driver 1A Dual TB6612FNG
  S1 = Reed switch [package=THT]  # not connected
  S3 = Pushbutton [package="[THT]"]
  S4 = Pushbutton [package="[THT]"]
  R4 = Resistor [tolerance=±5% resistance=3.3k package="0603 [SMD]"]  # not connected
  R5 = Resistor [tolerance=±5% resistance=3.3k package="0603 [SMD]"]
  R6 = Resistor [tolerance=±5% resistance=3.3k package="0603 [SMD]"]  # not connected
  R7 = Resistor [tolerance=±5% resistance=3.3k package="0603 [SMD]"]

nets:
  N1: Composant1.CHARGE, Composant3.11
  N2: Composant1.DONE, Composant3.12
  N3: Composant3.1, S4.Pin_1, S4.Pin_2
  N4: Composant3.0, S3.Pin_1, S3.Pin_2
  N5: Composant3.A5, Composant4.STBY
  N6: Composant3.A4, DS1.DQ
  N7: Composant3.A3, Composant4.AIN1
  N8: Composant3.A2, Composant4.AIN2
  N9: Composant3.A1, R5.Pin_1
  N10: Composant3.A0, R7.Pin_0
  GND: Composant3.GND, DS1.GND
  +3V3: Composant3.+3V3, DS1.VDD, R2.Pin_1
  N11: M1.pin_1, Composant4.A02
  N12: M1.pin_2, Composant4.A01
  N13: S2.pin_1, Composant4.GND
  N14: DS4.DQ, R2.Pin_0
  N15: S3.Pin_4, S4.Pin_3, S4.Pin_4

custom parts:
  Adafruit USB DC Solar LiPo Charger: Make your projects to go green this summer with our specialized USB/Solar Lithium Ion Polymer Battery charger! This charger is a very unique design, perfect for outdoor projects, or DIY iPod chargers. We've spent over a year testing and tinkering with this charger to come up with a plug and play solution to charging batteries with the sun and we're really pleased with what we ended up with.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
  Lithium Ion Battery Pack 3.7V 4400mAh: This lithium ion pack is made of 2 balanced 2200mAh cells for a total of 4400mA capacity! The cells are connected in parallel and spot-welded to a protection circuit that provides over-voltage, under-voltage and over-current protection. Each cell can provide 1A of current for about 4 hours so all together the peak current you can draw is a little over 1.5 Amps. Note that these batteries are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
  Adafruit Feather 32u4 RFM9xW LoRa: This is the Adafruit Feather 32u4 LoRa Radio (RFM9x) - our take on an microcontroller with a "Long Range (LoRa)" packet radio transceiver with built in USB and battery charging. Its an Adafruit Feather 32u4 with a 868/915 MHz radio module cooked in! Great for making wireless networks that can go further than 2.4GHz 802.15.4 and similar, are more flexible than Bluetooth LE and without the high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
